// Logisim project contunit.circ as structural Verilog: 17 circuits, main circuit main
module main (
);

  wire adder_1_out_3, adder_2_out_3, alu_1_out_4, alu_1_out_5, alu_1_out_6, alucont_1_out_3, alucont_1_out_4,
       and_1_out, and_2_out, control_unit_1_out_3, control_unit_1_out_4, control_unit_1_out_5,
       control_unit_1_out_6, control_unit_1_out_7, control_unit_1_out_8, control_unit_1_out_9,
       control_unit_1_out_10, control_unit_1_out_11, control_unit_1_out_12, control_unit_1_out_13,
       control_unit_1_out_14, datmem_1_out_5, instmem_1_out_2, jump_branchcontunit_1_out_8, mux2_1_out_5,
       mux2_2_out_5, mux2_3_out_5, mux2_4_out_5, mux2_5_out_5, mux2_6_out_5, mux4_1_out_6, mux_1_out_5,
       mux_2_out_5, or_1_out, or_2_out, or_3_out, pc_1_out_2, registerfile_1_out_6, registerfile_1_out_7,
       sext2_1_out_2, shiftleft2_2_out_2, sign_extend_1_out_2, undriven, undriven_2, undriven_3, undriven_4,
       undriven_5, undriven_6, undriven_7, zeroextend_1_out_2;

  pc pc_1 (.in_1(mux4_1_out_6), .out_2(pc_1_out_2));
  adder adder_1 (.in_1(pc_1_out_2), .in_2(undriven), .out_3(adder_1_out_3));
  instmem instmem_1 (.in_1(pc_1_out_2), .out_2(instmem_1_out_2));
  mux2 mux2_1 (
    .in_2(instmem_1_out_2), .in_3(instmem_1_out_2), .out_5(mux2_1_out_5), .in_1(control_unit_1_out_13));  // open: in_4
  sext2 sext2_1 (.in_1(instmem_1_out_2), .out_2(sext2_1_out_2));
  and and_1 (and_1_out, undriven_2, control_unit_1_out_6);
  shiftleft2 shiftleft2_1 (.in_1(sext2_1_out_2), .out_2(adder_1_out_3));
  or or_1 (or_1_out, undriven_4, undriven_5);
  and and_2 (and_2_out, or_1_out, control_unit_1_out_12);
  or or_2 (or_2_out, alucont_1_out_4, and_1_out, and_2_out);
  mux2 mux2_2 (.in_2(mux2_1_out_5), .in_3(undriven_3), .out_5(mux2_2_out_5), .in_1(or_2_out));  // open: in_4
  mux mux_1 (.in_2(adder_1_out_3), .in_3(mux_2_out_5), .out_5(mux_1_out_5), .in_1(or_2_out));  // open: in_4
  registerfile registerfile_1 (
    .in_2(control_unit_1_out_5), .in_3(instmem_1_out_2), .in_4(mux2_2_out_5), .in_5(mux_1_out_5),
    .out_6(registerfile_1_out_6), .out_7(registerfile_1_out_7), .in_1(instmem_1_out_2));
  sign_extend sign_extend_1 (.in_1(instmem_1_out_2), .out_2(sign_extend_1_out_2));
  zeroextend zeroextend_1 (.in_1(instmem_1_out_2), .out_2(zeroextend_1_out_2));
  control_unit control_unit_1 (
    .out_4(control_unit_1_out_4), .out_5(control_unit_1_out_5), .out_6(control_unit_1_out_6),
    .out_7(control_unit_1_out_7), .out_10(control_unit_1_out_10), .in_2(instmem_1_out_2),
    .out_12(control_unit_1_out_12), .out_13(control_unit_1_out_13), .out_14(control_unit_1_out_14),
    .out_9(control_unit_1_out_9), .out_11(control_unit_1_out_11), .out_8(control_unit_1_out_8),
    .out_3(control_unit_1_out_3), .in_1(instmem_1_out_2));
  mux2 mux2_3 (
    .in_2(sign_extend_1_out_2), .in_3(zeroextend_1_out_2), .out_5(mux2_3_out_5), .in_1(control_unit_1_out_14));  // open: in_4
  mux2 mux2_4 (
    .in_2(registerfile_1_out_7), .in_3(mux2_3_out_5), .out_5(mux2_4_out_5), .in_1(control_unit_1_out_7));  // open: in_4
  shiftleft2 shiftleft2_2 (.in_1(sign_extend_1_out_2), .out_2(shiftleft2_2_out_2));
  alucont alucont_1 (
    .in_1(control_unit_1_out_4), .in_2(instmem_1_out_2), .out_4(alucont_1_out_4), .out_3(alucont_1_out_3));
  mux2 mux2_5 (
    .in_2(mux2_4_out_5), .in_3(undriven_7), .out_5(mux2_5_out_5), .in_1(control_unit_1_out_12));  // open: in_4
  adder adder_2 (.in_1(adder_1_out_3), .in_2(shiftleft2_2_out_2), .out_3(adder_2_out_3));
  alu alu_1 (
    .in_1(registerfile_1_out_6), .in_2(mux2_5_out_5), .out_6(alu_1_out_6), .out_4(alu_1_out_4),
    .out_5(alu_1_out_5), .in_3(alucont_1_out_3));
  mux2 mux2_6 (.in_2(mux_2_out_5), .in_3(registerfile_1_out_6), .out_5(mux2_6_out_5), .in_1(and_1_out));  // open: in_4
  jump_branchcontunit jump_branchcontunit_1 (
    .in_2(control_unit_1_out_3), .in_3(control_unit_1_out_6), .in_5(control_unit_1_out_12),
    .in_6(control_unit_1_out_10), .in_7(control_unit_1_out_11), .out_8(jump_branchcontunit_1_out_8),
    .in_1(alu_1_out_5), .in_4(alu_1_out_4));
  datmem datmem_1 (
    .in_2(alu_1_out_6), .in_4(registerfile_1_out_7), .out_5(datmem_1_out_5), .in_1(control_unit_1_out_8),
    .in_3(undriven_6));
  mux4 mux4_1 (
    .in_1(mux2_6_out_5), .in_3(adder_2_out_3), .in_4(adder_1_out_3), .in_2(adder_1_out_3),
    .out_6(mux4_1_out_6), .in_5(jump_branchcontunit_1_out_8));
  or or_3 (or_3_out, control_unit_1_out_9, alucont_1_out_4);
  mux mux_2 (.in_2(datmem_1_out_5), .in_3(alu_1_out_6), .out_5(mux_2_out_5), .in_1(or_3_out));  // open: in_4

  // Notes on the sheet:
  //   4
  //   Inst[31-26]
  //   Inst[25-21]
  //   Inst[20-16]
  //   Inst[15-11]
  //   Inst[15-0]
  //   Inst[5-0]
  //   Inst[25-0]
  //   nout
  //   linkto31selectBit
  //   11111
  //   nout
  //   zout
  //   mult6
  //   mult8
  //   RegDest
  //   Andi
  //   concatenation =(PC+4)[31-28] concat Instruction[25-0] concat 00
  //   beqSignal
  //   balrnsignal
  //   blezsignal
  //   JalSignal,
  //   JmorSign
  //   MemToReg
  //   MemWrite
  //   ALUOp
  //   MemRead
  //   AluSrc
  //   RegWrite
  //   0
  //   shamt
  //   PC + 4 + Mem[rs]
  //   R[rs]
  //   PC+4+4*LABEL
  //   PC + 4
  //   4*LABEL
  //   mux7
endmodule

module control_unit (
  input  in_1,
  input  in_2,
  output out_3,
  output out_4,
  output out_5,
  output out_6,
  output out_7,
  output out_8,
  output out_9,
  output out_10,
  output out_11,
  output out_12,
  output out_13,
  output out_14
);
endmodule

module registerfile (
  input  in_1,
  input  in_2,
  input  in_3,
  input  in_4,
  input  in_5,
  output out_6,
  output out_7
);
endmodule

module datmem (
  input  in_1,
  input  in_2,
  input  in_3,
  input  in_4,
  output out_5
);
endmodule

module mux (
  input  in_1,
  input  in_2,
  input  in_3,
  input  in_4,
  output out_5
);
endmodule

module mux4 (
  input  in_1,
  input  in_2,
  input  in_3,
  input  in_4,
  input  in_5,
  output out_6
);
endmodule

module adder (
  input  in_1,
  input  in_2,
  output out_3
);
endmodule

module sign_extend (
  input  in_1,
  output out_2
);
endmodule

module zeroextend (
  input  in_1,
  output out_2
);
endmodule

module instmem (
  input  in_1,
  output out_2
);
endmodule

module alu (
  input  in_1,
  input  in_2,
  input  in_3,
  output out_4,
  output out_5,
  output out_6
);
endmodule

module pc (
  input  in_1,
  output out_2
);
endmodule

module shiftleft2 (
  input  in_1,
  output out_2
);
endmodule

module jump_branchcontunit (
  input  in_1,
  input  in_2,
  input  in_3,
  input  in_4,
  input  in_5,
  input  in_6,
  input  in_7,
  output out_8
);
endmodule

module mux2 (
  input  in_1,
  input  in_2,
  input  in_3,
  input  in_4,
  output out_5
);
endmodule

module alucont (
  input  in_1,
  input  in_2,
  output out_3,
  output out_4
);
endmodule

module sext2 (
  input  in_1,
  output out_2
);
endmodule
